# Fritzing sketch Control Temperatura LCD regulable (saved by Fritzing 0.9.3b)
breadboards: 1

parts:
  DHT11_1 = DHT11 module
  Componente1 = Arduino Uno (Rev3)
  KY-1 = Keyes Relay [package=THT]
  Componente2 = LCD1602-I2C
  R1 = Rotary Potentiometer (Small) [maximum_resistance=100kΩ package=THT]

nets:
  VCC: DHT11_1.VCC, Componente1.5V, KY-1.power, Componente2.VCC, R1.leg2
  GND: DHT11_1.GND, Componente1.GND, KY-1.ground, Componente2.GND, R1.leg1
  N1: DHT11_1.DATA, Componente1.D2
  N2: Componente1.A0, R1.wiper
  N3: Componente1.D8, KY-1.signal
  N4: Componente1.A4/SDA, Componente2.SDA
  N5: Componente1.A5/SCL, Componente2.SCL

custom parts:
  DHT11 module: DHT11 black pcb module
  Keyes Relay: The Keyes 5V relay module is suitable for SCM development, home appliance control. It uses a 5V~12V TIL control signal which can control DC / AC signal.
  LCD1602-I2C: A standard character display, usually with 2x16 characters. Comes in many colors with LCM1602 IIC attached.
